# Fritzing sketch CO2_wiring (saved by Fritzing 0.9.9b)
breadboards: 1

parts:
  Part1 = Arduino Uno (Rev3) - ICSP
  ZS-042_RTC1 = ZS-042 RTC Module
  Part2 = Adafruit MicroSD card breakout board [part_number="Adafruit #254"]
  Part3 = SCD30
  LED1 = RGB LED - (4 legs) [package="5 mm [THT]"]

nets:
  N1: Part1.A4/SDA, ZS-042_RTC1.SDA, Part3.RX/SDA
  N2: Part1.A5/SCL, ZS-042_RTC1.SCL, Part3.TX/SCL
  N3: Part1.ICSP_MOSI, Part1.D11_PWM/MOSI, Part2.DI
  N4: Part1.D10_PWM/SS, Part2.CS
  N5: Part1.D12/MISO, Part2.DO
  N6: Part1.D13/SCK, Part2.CLK
  GND: Part1.GND, ZS-042_RTC1.GND, Part2.GND, Part3.GND, LED1.green_cathode
  N7: Part1.D2, LED1.blue_cathode
  N8: Part1.D4, LED1.common_anode
  N9: Part1.D6_PWM, LED1.red_cathode
  3V3: Part1.3V3, Part3.VDD
  VCC: Part1.5V, ZS-042_RTC1.VCC, Part2.VCC

custom parts:
  Adafruit MicroSD card breakout board: Not just a simple breakout board, this microSD adapter goes the extra mile - designed for ease of use. Onboard 5v->3v regulator provides 150mA for power-hungry cards 3v level shifting means you can use this with ease on either 3v or 5v systems Uses a proper level shifting chip, not resistors: less problems, and faster read/write access Use 3 or 4 digital pins to read and write 2Gb+ of storage!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
  SCD30: CO2 , humidity, and temperature sensor * Current consumption: 19 mA @ 1 meas. per 2 s. * Digital interface UART or I2C * Company: Sensirion - The Sensor Company Electrical specifications * average current: 19 mA * max. current: 75 mA * DC supply: 3.3 V - 5.5 V Operation conditions * temperature: 0 – 50°C * humidity: 0 – 95 %RH * sensor lifetime: 15 years CO2-sensor: * NDIR CO 2 sensor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
